# Fritzing sketch Arduino1.2 LED (saved by Fritzing 0.9.10b)
breadboards: 1

parts:
  R1 = Resistor [tolerance=±5% power=0.25 resistance=220 package=THT]
  Componente1 = Arduino Uno (Rev3)
  LED1 = LED - 5mm [color="Red (633nm)" current=0.030 package="5 mm [THT]"]

nets:
  N1: R1.Pin_0, Componente1.GND
  N2: R1.Pin_1, LED1.cathode
  N3: Componente1.D2, LED1.anode
