# Fritzing sketch Arduino1.4 LED (saved by Fritzing 0.9.10b)
breadboards: 1

parts:
  R1 = Resistor [tolerance=±5% power=0.25 resistance=220 package=THT]
  Componente1 = Arduino Uno (Rev3)
  LED1 = LED - 5mm [color="Yellow (592nm)" current=0.030 package="5 mm [THT]"]
  LED2 = LED - 5mm [color="Green (565nm)" current=0.030 package="5 mm [THT]"]
  R2 = Resistor [tolerance=±5% power=0.25 resistance=220 package=THT]
  R3 = Resistor [tolerance=±5% power=0.25 resistance=220 package=THT]
  R4 = Resistor [tolerance=±5% power=0.25 resistance=220 package=THT]
  LED3 = LED - 5mm [color="Blue (470nm)" current=0.030 package="5 mm [THT]"]
  LED4 = LED - 5mm [color="Red (633nm)" current=0.030 package="5 mm [THT]"]

nets:
  N1: R1.Pin_0, Componente1.GND, R2.Pin_0, R3.Pin_0, R4.Pin_0
  N2: R1.Pin_1, LED2.cathode
  N3: Componente1.D2, LED2.anode
  N4: Componente1.D3_PWM, LED1.anode
  N5: Componente1.D4, LED4.anode
  N6: Componente1.D5_PWM, LED3.anode
  N7: LED1.cathode, R2.Pin_1
  N8: R3.Pin_1, LED3.cathode
  N9: R4.Pin_1, LED4.cathode
